# Fritzing sketch proj (saved by Fritzing 0.9.2b)

parts:
  Часть1 = Arduino Nano (Rev3.0)
  DFPlayer_Mini1 = DFPlayer MINI [package="DIP (Dual Inline) [THT]"]
  S1 = Momentary Switch [package=ksa_sealed_tac_switch]
  S2 = Momentary Switch [package=ksa_sealed_tac_switch]
  S3 = Momentary Switch [package=ksa_sealed_tac_switch]
  R1 = Resistor [tolerance=±5% resistance=220 package="0603 [SMD]"]

nets:
  GND: Часть1.GND, DFPlayer_Mini1.GND, R1.Pin_0
  N1: Часть1.D8, DFPlayer_Mini1.TX
  N2: Часть1.D9, DFPlayer_Mini1.RX
  5V: Часть1.5V, DFPlayer_Mini1.VCC, S3.3
  N3: Часть1.A3, S3.2
  N4: Часть1.A2, S2.2
  N5: Часть1.A1, S1.2
  N6: S3.1, R1.Pin_1

custom parts:
  DFPlayer MINI: MP3 module by DFRobot.com for playing Music from an SD-Card. Supports WAV and MP3 files.
